// Logisim project Practica2Etzael.circ as structural Verilog: 11 circuits, main circuit not
module \not  (
  input  in_1,
  output out_2
);

  Transistor transistor_1 (.in(1'b1), .out(out_2), .gate(in_1));
  Transistor #(.\type ("n")) transistor_2 (.in(1'b0), .out(out_2), .gate(in_1));
endmodule

module \and  (
  input  in_1,
  input  in_2,
  output out_3
);

  wire transistor_1_out;

  Transistor #(.\type ("n")) transistor_1 (.in(1'b1), .out(transistor_1_out), .gate(in_1));
  Transistor #(.\type ("n")) transistor_2 (.in(transistor_1_out), .out(out_3), .gate(in_2));
  Pull_Resistor pull_resistor_1 (.node(out_3));
endmodule

module \or  (
  input  in_1,
  input  in_2,
  output out_3
);

  wire pull_resistor_1_node;

  Transistor #(.\type ("n")) transistor_1 (.in(1'b1), .out(out_3), .gate(in_1));
  Transistor #(.\type ("n")) transistor_2 (.in(pull_resistor_1_node), .out(out_3), .gate(in_2));
  Pull_Resistor #(.pull(1)) pull_resistor_1 (.node(pull_resistor_1_node));
  Pull_Resistor pull_resistor_2 (.node(out_3));
endmodule

module \xor  (
  input  in_1,
  input  in_2,
  output out_3
);

  wire and_out_3, not_out_2, or_out_3;

  \not  \not  (.in_1(and_out_3), .out_2(not_out_2));
  \and  \and  (.in_1(in_1), .in_2(in_2), .out_3(and_out_3));
  \or  \or  (.in_1(in_1), .in_2(in_2), .out_3(or_out_3));
  \and  and_2 (.in_1(not_out_2), .in_2(or_out_3), .out_3(out_3));
endmodule

module equiv (
  input  in_1,
  input  in_2,
  output out_3
);

  wire xor_out_3;

  \xor  \xor  (.in_1(in_1), .in_2(in_2), .out_3(xor_out_3));
  \not  \not  (.in_1(xor_out_3), .out_2(out_3));
endmodule

module and3 (
  input  in_1,
  input  in_2,
  input  in_3,
  output out_4
);

  wire and_out_3;

  \and  \and  (.in_1(in_1), .in_2(in_2), .out_3(and_out_3));
  \and  and_2 (.in_1(and_out_3), .in_2(in_3), .out_3(out_4));
endmodule

module primos (
  input  in_1,
  input  in_2,
  input  in_3,
  input  in_4,
  output out_5
);

  wire and3_2_out_4, and3_3_out_4, and3_4_out_4, and3_out_4, not_2_out_2, not_3_out_2, not_out_2, or_2_out_3,
       or_out_3;

  \not  \not  (.in_1(in_1), .out_2(not_out_2));
  \not  not_2 (.in_1(in_2), .out_2(not_2_out_2));
  \not  not_3 (.in_1(in_3), .out_2(not_3_out_2));
  and3 and3 (.in_1(not_out_2), .in_2(in_2), .in_3(in_4), .out_4(and3_out_4));
  and3 and3_2 (.in_1(not_out_2), .in_2(not_2_out_2), .in_3(in_3), .out_4(and3_2_out_4));
  and3 and3_3 (.in_1(in_2), .in_2(not_3_out_2), .in_3(in_4), .out_4(and3_3_out_4));
  and3 and3_4 (.in_1(not_2_out_2), .in_2(in_3), .in_3(in_4), .out_4(and3_4_out_4));
  \or  \or  (.in_1(and3_out_4), .in_2(and3_2_out_4), .out_3(or_out_3));
  \or  or_2 (.in_1(and3_3_out_4), .in_2(and3_4_out_4), .out_3(or_2_out_3));
  \or  or_3 (.in_1(or_out_3), .in_2(or_2_out_3), .out_3(out_5));
endmodule

module mini (
  input  in_1,
  input  in_2,
  input  in_3,
  output out_4
);

  wire and3_2_out_4, and3_out_4, and_out_3, not_2_out_2, not_out_2, or_2_out_3;

  \not  \not  (.in_1(in_1), .out_2(not_out_2));
  \not  not_2 (.in_1(in_2), .out_2(not_2_out_2));
  \and  \and  (.in_1(not_out_2), .in_2(not_2_out_2), .out_3(and_out_3));
  and3 and3 (.in_1(not_out_2), .in_2(in_2), .in_3(in_3), .out_4(and3_out_4));
  and3 and3_2 (.in_1(in_1), .in_2(not_2_out_2), .in_3(in_3), .out_4(and3_2_out_4));
  \or  \or  (.in_1(and_out_3), .in_2(or_2_out_3), .out_3(out_4));
  \or  or_2 (.in_1(and3_out_4), .in_2(and3_2_out_4), .out_3(or_2_out_3));
endmodule

module maxi (
  input  in_1,
  input  in_2,
  input  in_3,
  output out_4
);

  wire not_2_out_2, not_3_out_2, not_out_2, or3_2_out_4, or3_out_4, or_out_3;

  \not  \not  (.in_1(in_1), .out_2(not_out_2));
  \not  not_2 (.in_1(in_2), .out_2(not_2_out_2));
  \not  not_3 (.in_1(in_3), .out_2(not_3_out_2));
  or3 or3 (.in_1(not_out_2), .in_2(not_2_out_2), .in_3(not_3_out_2), .out_4(or3_out_4));
  or3 or3_2 (.in_1(not_out_2), .in_2(in_2), .in_3(in_3), .out_4(or3_2_out_4));
  \or  \or  (.in_1(not_2_out_2), .in_2(in_3), .out_3(or_out_3));
  and3 and3 (.in_1(or3_out_4), .in_2(or3_2_out_4), .in_3(or_out_3), .out_4(out_4));
endmodule

module or3 (
  input  in_1,
  input  in_2,
  input  in_3,
  output out_4
);

  wire or_out_3;

  \or  \or  (.in_1(in_1), .in_2(in_2), .out_3(or_out_3));
  \or  or_2 (.in_1(or_out_3), .in_2(in_3), .out_3(out_4));
endmodule

module planta (
  input  in_1,
  input  in_2,
  input  in_3,
  output out_4,
  output out_5,
  output out_6
);

  wire and3_2_out_4, and3_3_out_4, and3_4_out_4, and3_5_out_4, and3_6_out_4, and3_out_4, not_2_out_2,
       not_3_out_2, not_out_2;

  \not  \not  (.in_1(in_1), .out_2(not_out_2));
  \not  not_2 (.in_1(in_2), .out_2(not_2_out_2));
  \not  not_3 (.in_1(in_3), .out_2(not_3_out_2));
  and3 and3 (.in_1(not_out_2), .in_2(in_2), .in_3(in_3), .out_4(and3_out_4));
  and3 and3_2 (.in_1(in_1), .in_2(not_2_out_2), .in_3(in_3), .out_4(and3_2_out_4));
  and3 and3_3 (.in_1(in_1), .in_2(in_2), .in_3(not_3_out_2), .out_4(and3_3_out_4));
  and3 and3_4 (.in_1(not_out_2), .in_2(not_2_out_2), .in_3(in_3), .out_4(and3_4_out_4));
  and3 and3_5 (.in_1(not_out_2), .in_2(in_2), .in_3(not_3_out_2), .out_4(and3_5_out_4));
  and3 and3_6 (.in_1(in_1), .in_2(not_2_out_2), .in_3(not_3_out_2), .out_4(and3_6_out_4));
  or3 or3 (.in_1(and3_4_out_4), .in_2(and3_5_out_4), .in_3(and3_6_out_4), .out_4(out_4));
  or3 or3_2 (.in_1(and3_out_4), .in_2(and3_2_out_4), .in_3(and3_3_out_4), .out_4(out_5));
  and3 and3_7 (.in_1(in_1), .in_2(in_2), .in_3(in_3), .out_4(out_6));
endmodule
