// Logisim project Practica3.circ as structural Verilog: 9 circuits, main circuit semi
module semi (
  input  in_1,
  input  in_2,
  output out_3,
  output out_4
);

  xor xor_1 (out_3, in_1, in_2);
  and and_1 (out_4, in_1, in_2);
endmodule

module completo (
  input  in_1,
  input  in_2,
  input  in_3,
  output out_4,
  output out_5
);

  wire semi_2_out_4, semi_out_3, semi_out_4;

  semi semi (.in_1(in_1), .in_2(in_2), .out_3(semi_out_3), .out_4(semi_out_4));
  semi semi_2 (.in_1(semi_out_3), .in_2(in_3), .out_3(out_4), .out_4(semi_2_out_4));
  or or_1 (out_5, semi_2_out_4, semi_out_4);
endmodule

module resta (
  input  in_1,
  input  [7:0] in_2,
  input  [7:0] in_3,
  output [7:0] out_4,
  output out_5
);

  wire [7:0] multiplexer_1_out, not_1_out;

  assign not_1_out = ~in_3;  // NOT_Gate not_1, 8 bits wide
  Multiplexer #(.width(8), .enable("false")) multiplexer_1 (
    .in0(in_3), .in1(not_1_out), .out(multiplexer_1_out), .sel(in_1));
  Ejercicio2 ejercicio2_1 (.A(in_2), .B(multiplexer_1_out), .out_5(out_4), .in_2(in_1), .in_1(2'b11), .out_6(out_5));
endmodule

module comparador (
  input  [7:0] in_1,
  input  [7:0] in_2,
  output [7:0] out_3,
  output [7:0] out_4,
  output [7:0] out_5
);

  wire not_1_out, not_2_out;
  wire [6:0] resta_1_out_4;

  resta resta_1 (.in_2(in_1), .in_3(in_2), .in_1(1'b1), .out_4({out_5[0], resta_1_out_4}));  // open: out_5
  nor nor_1 (out_3[0], resta_1_out_4[0], resta_1_out_4[1], resta_1_out_4[2], resta_1_out_4[3], resta_1_out_4[4], resta_1_out_4[5], resta_1_out_4[6], out_5[0]);
  not not_1 (not_1_out, out_3[0]);
  not not_2 (not_2_out, out_5[0]);
  and and_1 (out_4[0], not_1_out, not_2_out);

  assign out_3[7:1] = {7{1'b0}};
  assign out_4[7:1] = {7{1'b0}};
  assign out_5[7:1] = {7{1'b0}};
endmodule

module Ejercicio1 (
  input  in_1,
  input  in_2,
  input  in_3,
  input  [1:0] in_4,
  output out_5,
  output out_6
);

  wire and_1_out, and_2_out, completo_1_out_4, completo_1_out_5, not_1_out, or_1_out;

  or or_1 (or_1_out, in_3, in_2);
  and and_1 (and_1_out, in_3, in_2);
  not not_1 (not_1_out, in_2);
  completo completo_1 (.in_1(in_2), .in_2(in_3), .in_3(in_1), .out_4(completo_1_out_4), .out_5(completo_1_out_5));
  and and_2 (and_2_out, in_4[1], in_4[0]);
  and and_3 (out_6, completo_1_out_5, and_2_out);
  Multiplexer #(.select(2), .enable("false")) multiplexer_1 (
    .in0(and_1_out), .in1(or_1_out), .in2(not_1_out), .in3(completo_1_out_4), .out(out_5), .sel(in_4));
endmodule

module Ejercicio2 (
  input  [1:0] in_1,
  input  in_2,
  input  [7:0] A,
  input  [7:0] B,
  output [7:0] out_5,
  output out_6
);

  wire ejercicio1_1_out_6, ejercicio1_2_out_6, ejercicio1_3_out_6, ejercicio1_4_out_6, ejercicio1_5_out_6,
       ejercicio1_6_out_6, ejercicio1_7_out_6;

  Ejercicio1 ejercicio1_1 (
    .in_2(A[0]), .in_3(B[0]), .out_5(out_5[0]), .in_1(in_2), .in_4(in_1), .out_6(ejercicio1_1_out_6));
  Ejercicio1 ejercicio1_2 (
    .in_2(A[1]), .in_3(B[1]), .out_5(out_5[1]), .in_1(ejercicio1_1_out_6), .in_4(in_1),
    .out_6(ejercicio1_2_out_6));
  Ejercicio1 ejercicio1_3 (
    .in_2(A[2]), .in_3(B[2]), .out_5(out_5[2]), .in_1(ejercicio1_2_out_6), .in_4(in_1),
    .out_6(ejercicio1_3_out_6));
  Ejercicio1 ejercicio1_4 (
    .in_2(A[3]), .in_3(B[3]), .out_5(out_5[3]), .in_1(ejercicio1_3_out_6), .in_4(in_1),
    .out_6(ejercicio1_4_out_6));
  Ejercicio1 ejercicio1_5 (
    .in_2(A[4]), .in_3(B[4]), .out_5(out_5[4]), .in_1(ejercicio1_4_out_6), .in_4(in_1),
    .out_6(ejercicio1_5_out_6));
  Ejercicio1 ejercicio1_6 (
    .in_2(A[5]), .in_3(B[5]), .out_5(out_5[5]), .in_1(ejercicio1_5_out_6), .in_4(in_1),
    .out_6(ejercicio1_6_out_6));
  Ejercicio1 ejercicio1_7 (
    .in_2(A[6]), .in_3(B[6]), .out_5(out_5[6]), .in_1(ejercicio1_6_out_6), .in_4(in_1),
    .out_6(ejercicio1_7_out_6));
  Ejercicio1 ejercicio1_8 (
    .in_2(A[7]), .in_3(B[7]), .out_5(out_5[7]), .in_1(ejercicio1_7_out_6), .in_4(in_1), .out_6(out_6));
endmodule

module Ejercicio3 (
  input  [2:0] in_1,
  input  in_2,
  input  [7:0] A,
  input  [7:0] B,
  output [7:0] out_5,
  output out_6
);

  wire and_1_out, ejercicio1_1_out_6, ejercicio1_2_out_6, ejercicio1_3_out_6, ejercicio1_4_out_6,
       ejercicio1_5_out_6, ejercicio1_6_out_6, ejercicio1_7_out_6, ejercicio1_8_out_6, resta_1_out_5;
  wire [7:0] ejercicio1_1_out_5, resta_1_out_4;

  Ejercicio1 ejercicio1_1 (
    .in_2(A[0]), .in_3(B[0]), .out_5(ejercicio1_1_out_5[0]), .in_1(in_2), .in_4(in_1[1:0]),
    .out_6(ejercicio1_1_out_6));
  Ejercicio1 ejercicio1_2 (
    .in_2(A[1]), .in_3(B[1]), .out_5(ejercicio1_1_out_5[1]), .in_1(ejercicio1_1_out_6), .in_4(in_1[1:0]),
    .out_6(ejercicio1_2_out_6));
  Ejercicio1 ejercicio1_3 (
    .in_2(A[2]), .in_3(B[2]), .out_5(ejercicio1_1_out_5[2]), .in_1(ejercicio1_2_out_6), .in_4(in_1[1:0]),
    .out_6(ejercicio1_3_out_6));
  Ejercicio1 ejercicio1_4 (
    .in_2(A[3]), .in_3(B[3]), .out_5(ejercicio1_1_out_5[3]), .in_1(ejercicio1_3_out_6), .in_4(in_1[1:0]),
    .out_6(ejercicio1_4_out_6));
  Ejercicio1 ejercicio1_5 (
    .in_2(A[4]), .in_3(B[4]), .out_5(ejercicio1_1_out_5[4]), .in_1(ejercicio1_4_out_6), .in_4(in_1[1:0]),
    .out_6(ejercicio1_5_out_6));
  Ejercicio1 ejercicio1_6 (
    .in_2(A[5]), .in_3(B[5]), .out_5(ejercicio1_1_out_5[5]), .in_1(ejercicio1_5_out_6), .in_4(in_1[1:0]),
    .out_6(ejercicio1_6_out_6));
  Ejercicio1 ejercicio1_7 (
    .in_2(A[6]), .in_3(B[6]), .out_5(ejercicio1_1_out_5[6]), .in_1(ejercicio1_6_out_6), .in_4(in_1[1:0]),
    .out_6(ejercicio1_7_out_6));
  Ejercicio1 ejercicio1_8 (
    .in_2(A[7]), .in_3(B[7]), .out_5(ejercicio1_1_out_5[7]), .in_1(ejercicio1_7_out_6), .in_4(in_1[1:0]),
    .out_6(ejercicio1_8_out_6));
  Multiplexer #(.enable("false")) multiplexer_1 (
    .in0(ejercicio1_8_out_6), .in1(resta_1_out_5), .out(out_6), .sel(and_1_out));
  resta resta_1 (.in_2(A), .in_3(B), .in_1(and_1_out), .out_5(resta_1_out_5), .out_4(resta_1_out_4));
  and and_1 (and_1_out, in_1[0], in_1[1], in_1[2]);
  Multiplexer #(.width(8), .enable("false")) multiplexer_2 (
    .in0(ejercicio1_1_out_5), .in1(resta_1_out_4), .out(out_5), .sel(and_1_out));
endmodule

module Ejercicio4 (
  input  [2:0] in_1,
  input  in_2,
  input  [7:0] A,
  input  [7:0] B,
  output [7:0] out_5,
  output out_6
);

  wire and_1_out, ejercicio1_1_out_6, ejercicio1_2_out_6, ejercicio1_3_out_6, ejercicio1_4_out_6,
       ejercicio1_5_out_6, ejercicio1_6_out_6, ejercicio1_7_out_6, ejercicio1_8_out_6, resta_1_out_5;
  wire [7:0] comparador_1_out_3, comparador_1_out_4, comparador_1_out_5, ejercicio1_1_out_5,
       multiplexer_3_out, resta_1_out_4;

  Ejercicio1 ejercicio1_1 (
    .in_2(A[0]), .in_3(B[0]), .out_5(ejercicio1_1_out_5[0]), .in_1(in_2), .in_4(in_1[1:0]),
    .out_6(ejercicio1_1_out_6));
  Ejercicio1 ejercicio1_2 (
    .in_2(A[1]), .in_3(B[1]), .out_5(ejercicio1_1_out_5[1]), .in_1(ejercicio1_1_out_6), .in_4(in_1[1:0]),
    .out_6(ejercicio1_2_out_6));
  Ejercicio1 ejercicio1_3 (
    .in_2(A[2]), .in_3(B[2]), .out_5(ejercicio1_1_out_5[2]), .in_1(ejercicio1_2_out_6), .in_4(in_1[1:0]),
    .out_6(ejercicio1_3_out_6));
  Ejercicio1 ejercicio1_4 (
    .in_2(A[3]), .in_3(B[3]), .out_5(ejercicio1_1_out_5[3]), .in_1(ejercicio1_3_out_6), .in_4(in_1[1:0]),
    .out_6(ejercicio1_4_out_6));
  Ejercicio1 ejercicio1_5 (
    .in_2(A[4]), .in_3(B[4]), .out_5(ejercicio1_1_out_5[4]), .in_1(ejercicio1_4_out_6), .in_4(in_1[1:0]),
    .out_6(ejercicio1_5_out_6));
  Ejercicio1 ejercicio1_6 (
    .in_2(A[5]), .in_3(B[5]), .out_5(ejercicio1_1_out_5[5]), .in_1(ejercicio1_5_out_6), .in_4(in_1[1:0]),
    .out_6(ejercicio1_6_out_6));
  Ejercicio1 ejercicio1_7 (
    .in_2(A[6]), .in_3(B[6]), .out_5(ejercicio1_1_out_5[6]), .in_1(ejercicio1_6_out_6), .in_4(in_1[1:0]),
    .out_6(ejercicio1_7_out_6));
  Ejercicio1 ejercicio1_8 (
    .in_2(A[7]), .in_3(B[7]), .out_5(ejercicio1_1_out_5[7]), .in_1(ejercicio1_7_out_6), .in_4(in_1[1:0]),
    .out_6(ejercicio1_8_out_6));
  Multiplexer #(.enable("false")) multiplexer_1 (
    .in0(ejercicio1_8_out_6), .in1(resta_1_out_5), .out(out_6), .sel(and_1_out));
  and and_1 (and_1_out, in_1[0], in_1[1], in_1[2]);
  resta resta_1 (.in_2(A), .in_3(B), .in_1(and_1_out), .out_5(resta_1_out_5), .out_4(resta_1_out_4));
  comparador comparador_1 (
    .in_1(A), .in_2(B), .out_3(comparador_1_out_3), .out_4(comparador_1_out_4), .out_5(comparador_1_out_5));
  Multiplexer #(.width(8), .enable("false")) multiplexer_2 (
    .in0(ejercicio1_1_out_5), .in1(multiplexer_3_out), .out(out_5), .sel(in_1[2]));
  Multiplexer #(.select(2), .width(8), .enable("false")) multiplexer_3 (
    .in0(comparador_1_out_5), .in1(comparador_1_out_4), .in2(comparador_1_out_3), .in3(resta_1_out_4),
    .out(multiplexer_3_out), .sel(in_1[1:0]));
endmodule

module Ejercicio_5 (
  input  [2:0] in_1,
  input  in_2,
  input  [7:0] in_3,
  input  [7:0] in_4,
  output [7:0] out_5,
  output out_6
);

  // Ejercicio4 ejercicio4_1: pin names not known; wires that end beside it: in_3, in_4, in_2, out_6, in_1, out_5
endmodule
