// Logisim project Practica4.circ as structural Verilog: 5 circuits, main circuit Ejercicio1
module Flip_flop_D (
  input  in_1,
  input  in_2,
  output out_3,
  output out_4
);

  wire not_1_out;

  S_R_Flip_Flop s_r_ff_1 (.S(in_1), .clk(in_2), .R(not_1_out), .Q(out_3), .Qn(out_4));  // open: preset, reset, en
  not not_1 (not_1_out, in_1);
endmodule

module Ejercicio1 (
  input  x,
  output [1:0] out_2,
  output out_3
);

  wire and_1_out, and_2_out, and_3_out, and_4_out, clock_1_out, not_1_out, not_2_out, not_3_out;

  not not_1 (not_1_out, x);
  not not_2 (not_2_out, out_2[1]);
  not not_3 (not_3_out, out_2[0]);
  Clock clock_1 (.out(clock_1_out));
  and and_1 (and_1_out, not_1_out, not_2_out);
  and and_2 (and_2_out, not_1_out, out_2[1]);
  and and_3 (and_3_out, x, not_3_out);
  and and_4 (and_4_out, x, out_2[0]);
  J_K_Flip_Flop A (.J(and_1_out), .clk(clock_1_out), .K(and_2_out), .Q(out_2[1]));  // open: Qn, preset, en, reset
  J_K_Flip_Flop B (.J(and_3_out), .clk(clock_1_out), .K(and_4_out), .Q(out_2[0]));  // open: Qn, preset, en, reset
  nor nor_1 (out_3, out_2[0], out_2[1]);
endmodule

module Ejercicio2 (
  input  [7:0] in_1,
  input  in_2,
  output [7:0] out_3
);

  Flip_flop_D flip_flop_d_1 (.in_1(in_1[0]), .in_2(in_2), .out_3(out_3[0]));  // open: out_4
  Flip_flop_D flip_flop_d_2 (.in_1(in_1[1]), .in_2(in_2), .out_3(out_3[1]));  // open: out_4
  Flip_flop_D flip_flop_d_3 (.in_1(in_1[2]), .in_2(in_2), .out_3(out_3[2]));  // open: out_4
  Flip_flop_D flip_flop_d_4 (.in_1(in_1[3]), .in_2(in_2), .out_3(out_3[3]));  // open: out_4
  Flip_flop_D flip_flop_d_5 (.in_1(in_1[4]), .in_2(in_2), .out_3(out_3[4]));  // open: out_4
  Flip_flop_D flip_flop_d_6 (.in_1(in_1[5]), .in_2(in_2), .out_3(out_3[5]));  // open: out_4
  Flip_flop_D flip_flop_d_7 (.in_1(in_1[6]), .in_2(in_2), .out_3(out_3[6]));  // open: out_4
  Flip_flop_D flip_flop_d_8 (.in_1(in_1[7]), .in_2(in_2), .out_3(out_3[7]));  // open: out_4
endmodule

module Ejercicio3 (
  input  [1:0] in_1,
  input  [1:0] in_2,
  input  [1:0] in_3,
  input  [7:0] in_4,
  input  in_5,
  output [7:0] out_6,
  output [7:0] out_7
);

  wire [7:0] demultiplexer_1_out0, demultiplexer_1_out1, demultiplexer_1_out2, demultiplexer_1_out3,
       ejercicio2_1_out_3, ejercicio2_2_out_3, ejercicio2_3_out_3, ejercicio2_4_out_3;

  Demultiplexer #(.select(2), .width(8), .enable("false")) demultiplexer_1 (
    .out0(demultiplexer_1_out0), .out1(demultiplexer_1_out1), .out2(demultiplexer_1_out2),
    .out3(demultiplexer_1_out3), .in(in_4), .sel(in_3));
  Ejercicio2 ejercicio2_1 (.in_1(demultiplexer_1_out0), .out_3(ejercicio2_1_out_3), .in_2(in_5));
  Ejercicio2 ejercicio2_2 (.in_1(demultiplexer_1_out1), .out_3(ejercicio2_2_out_3), .in_2(in_5));
  Ejercicio2 ejercicio2_3 (.in_1(demultiplexer_1_out2), .out_3(ejercicio2_3_out_3), .in_2(in_5));
  Ejercicio2 ejercicio2_4 (.in_1(demultiplexer_1_out3), .out_3(ejercicio2_4_out_3), .in_2(in_5));
  Multiplexer #(.select(2), .width(8), .enable("false")) multiplexer_1 (
    .in0(ejercicio2_1_out_3), .in1(ejercicio2_2_out_3), .in2(ejercicio2_3_out_3), .in3(ejercicio2_4_out_3),
    .out(out_6), .sel(in_1));
  Multiplexer #(.select(2), .width(8), .enable("false")) multiplexer_2 (
    .in0(ejercicio2_1_out_3), .in1(ejercicio2_2_out_3), .in2(ejercicio2_3_out_3), .in3(ejercicio2_4_out_3),
    .out(out_7), .sel(in_2));
endmodule

module Ejercicio4 (
  input  [15:0] in_1,
  input  in_2,
  output [7:0] out_3,
  output out_4
);

  wire [7:0] ejercicio3_1_out_6, ejercicio3_1_out_7, multiplexer_1_out;

  Ejercicio3 ejercicio3_1 (
    .in_1(in_1[9:8]), .in_2(in_1[7:6]), .in_3(in_1[11:10]), .in_4(out_3), .in_5(in_2),
    .out_6(ejercicio3_1_out_6), .out_7(ejercicio3_1_out_7));
  Multiplexer #(.width(8), .enable("false")) multiplexer_1 (
    .in0(ejercicio3_1_out_7), .in1(in_1[7:0]), .out(multiplexer_1_out), .sel(in_1[12]));
  Practica3_Ejercicio4 ejercicio4_1 (
    .A(ejercicio3_1_out_6), .B(multiplexer_1_out), .out_5(out_3), .in_1(in_1[15:13]), .out_6(out_4),
    .in_2(1'b0));
endmodule
