// Logisim project Ejercicios.circ as structural Verilog: 11 circuits, main circuit equiv
module equiv (
  input  in_1,
  input  in_2,
  output Equiv
);

  xnor xnor_1 (Equiv, in_1, in_2);
endmodule

module Impl (
  input  in_1,
  input  in_2,
  output Impl
);

  wire not_1_out;

  not not_1 (not_1_out, in_1);
  or or_1 (Impl, not_1_out, in_2);
endmodule

module half_adder (
  input  in_1,
  input  in_2,
  output out_3,
  output out_4
);

  xor xor_1 (out_3, in_1, in_2);
  and and_1 (out_4, in_1, in_2);
endmodule

module full_adder (
  input  in_1,
  input  in_2,
  input  in_3,
  output out_4,
  output out_5
);

  wire and_1_out, and_2_out, xor_1_out;

  xor xor_1 (xor_1_out, in_1, in_2);
  xor xor_2 (out_4, xor_1_out, in_3);
  and and_1 (and_1_out, in_3, xor_1_out);
  and and_2 (and_2_out, in_1, in_2);
  or or_1 (out_5, and_1_out, and_2_out);
endmodule

module sumador4bits (
  input  [3:0] in_1,
  input  [3:0] in_2,
  output [3:0] out_3,
  output out_4
);

  wire full_adder_2_out_5, full_adder_out_5, half_adder_out_4;

  half_adder half_adder (.in_1(in_1[0]), .in_2(in_2[0]), .out_3(out_3[0]), .out_4(half_adder_out_4));
  full_adder full_adder (
    .in_1(half_adder_out_4), .in_2(in_1[1]), .in_3(in_2[1]), .out_4(out_3[1]), .out_5(full_adder_out_5));
  full_adder full_adder_2 (
    .in_1(full_adder_out_5), .in_2(in_1[2]), .in_3(in_2[2]), .out_4(out_3[2]), .out_5(full_adder_2_out_5));
  full_adder full_adder_3 (.in_1(full_adder_2_out_5), .in_2(in_1[3]), .in_3(in_2[3]), .out_4(out_3[3]), .out_5(out_4));
endmodule

module Ejercicio1 (
  input  P,
  input  Q,
  input  P_2,
  input  Q_2,
  input  P_3,
  input  Q_3,
  input  R,
  input  P_4,
  input  Q_4,
  input  R_2,
  output out_11,
  output out_12,
  output out_13,
  output out_14
);

  wire and_1_out, and_2_out, and_3_out, impl_2_impl, impl_3_impl, impl_4_impl, nand_1_out, not_1_out,
       not_2_out, or_1_out, or_2_out, or_3_out;

  not not_1 (not_1_out, P);
  not not_2 (not_2_out, Q);
  and and_1 (and_1_out, P_2, Q_2);
  and and_2 (and_2_out, P_3, Q_3);
  nand nand_1 (nand_1_out, P, Q);
  or or_1 (or_1_out, not_1_out, not_2_out);
  or or_2 (or_2_out, P_2, and_1_out);
  or or_3 (or_3_out, and_2_out, R);
  Impl impl_1 (.in_1(or_3_out), .in_2(Q_3), .Impl(out_13));
  Impl impl_2 (.in_1(P_4), .in_2(Q_4), .Impl(impl_2_impl));
  and and_3 (and_3_out, impl_2_impl, impl_3_impl);
  Impl impl_3 (.in_1(Q_4), .in_2(R_2), .Impl(impl_3_impl));
  Impl impl_4 (.in_1(P_4), .in_2(R_2), .Impl(impl_4_impl));
  equiv equiv_1 (.in_1(nand_1_out), .in_2(or_1_out), .Equiv(out_11));
  equiv equiv_2 (.in_1(P_2), .in_2(or_2_out), .Equiv(out_12));
  Impl impl_5 (.in_1(and_3_out), .in_2(impl_4_impl), .Impl(out_14));
endmodule

module Ejercicio2 (
  input  A,
  input  B,
  input  A_2,
  input  B_2,
  input  A_3,
  output out_6,
  output OR,
  output NOT
);

  wire nand_1_out, nand_2_out, nand_4_out;

  nand nand_1 (nand_1_out, A_2, A_2);
  nand nand_2 (nand_2_out, B_2, B_2);
  nand nand_3 (NOT, A_3, A_3);
  nand nand_4 (nand_4_out, A, B);
  nand nand_5 (out_6, nand_4_out, nand_4_out);
  nand nand_6 (OR, nand_1_out, nand_2_out);

  // Notes on the sheet:
  //   AND
endmodule

module Ejercicio3 (
  input  x,
  input  y,
  input  w,
  input  z,
  output out_5
);

  wire pull_resistor_1_node, pull_resistor_2_node, pull_resistor_3_node, pull_resistor_4_node,
       transistor_2_out, transistor_4_out;

  Pull_Resistor #(.pull(1)) pull_resistor_1 (.node(pull_resistor_1_node));
  Transistor #(.\type ("n")) transistor_1 (.in(transistor_2_out), .out(pull_resistor_1_node), .gate(x));
  Transistor #(.\type ("n")) transistor_2 (.in(1'b0), .out(transistor_2_out), .gate(y));
  Pull_Resistor #(.pull(1)) pull_resistor_2 (.node(pull_resistor_2_node));
  Transistor #(.\type ("n")) transistor_3 (.in(transistor_4_out), .out(pull_resistor_2_node), .gate(w));
  Transistor #(.\type ("n")) transistor_4 (.in(1'b0), .out(transistor_4_out), .gate(z));
  Pull_Resistor #(.pull(1)) pull_resistor_3 (.node(pull_resistor_3_node));
  Transistor #(.\type ("n")) transistor_5 (.in(1'b0), .out(pull_resistor_3_node), .gate(pull_resistor_1_node));
  Pull_Resistor #(.pull(1)) pull_resistor_4 (.node(pull_resistor_4_node));
  Transistor #(.\type ("n")) transistor_6 (.in(1'b0), .out(pull_resistor_4_node), .gate(pull_resistor_2_node));
  Pull_Resistor #(.pull(1)) pull_resistor_5 (.node(out_5));
  Transistor #(.\type ("n")) transistor_7 (.in(1'b0), .out(out_5), .gate(pull_resistor_3_node));
  Transistor #(.\type ("n")) transistor_8 (.in(1'b0), .out(out_5), .gate(pull_resistor_4_node));
endmodule

module Ejercicio4 (
  input  x,
  input  y,
  input  w,
  input  z,
  output out_5
);

  wire nand_1_out, nand_2_out, not_1_out, not_2_out;

  not not_1 (not_1_out, nand_1_out);
  nand nand_1 (nand_1_out, x, y);
  not not_2 (not_2_out, nand_2_out);
  nand nand_2 (nand_2_out, w, z);
  nor nor_1 (out_5, not_1_out, not_2_out);
endmodule

module Ejercicio8 (
  input  [3:0] in_1,
  input  [3:0] in_2,
  output [7:0] out_3
);

  wire [2:0] and_15_out;
  wire [3:0] and_10_out, and_11_out, and_12_out;
  wire [3:1] sumador_2_out_3, sumador_out_3;
  wire [3:3] sumador_2_out_4, sumador_out_4;

  and and_1 (and_10_out[3], in_2[1], in_1[3]);
  and and_2 (and_11_out[3], in_2[2], in_1[3]);
  and and_3 (and_12_out[3], in_2[3], in_1[3]);
  and and_4 (and_10_out[1], in_2[1], in_1[1]);
  and and_5 (and_10_out[2], in_2[1], in_1[2]);
  and and_6 (and_11_out[2], in_2[2], in_1[2]);
  and and_7 (and_11_out[1], in_2[2], in_1[1]);
  and and_8 (and_12_out[2], in_2[3], in_1[2]);
  and and_9 (and_12_out[1], in_2[3], in_1[1]);
  and and_10 (and_10_out[0], in_2[1], in_1[0]);
  and and_11 (and_11_out[0], in_2[2], in_1[0]);
  and and_12 (and_12_out[0], in_2[3], in_1[0]);
  and and_13 (and_15_out[2], in_2[0], in_1[3]);
  and and_14 (and_15_out[1], in_2[0], in_1[2]);
  sumador4bits sumador (
    .in_1({1'b0, and_15_out}), .in_2(and_10_out), .out_4(sumador_out_4[3]), .out_3({sumador_out_3, out_3[1]}));
  and and_15 (and_15_out[0], in_2[0], in_1[1]);
  and and_16 (out_3[0], in_2[0], in_1[0]);
  sumador4bits sumador_2 (
    .in_1({sumador_out_4[3], sumador_out_3}), .in_2(and_11_out), .out_4(sumador_2_out_4[3]),
    .out_3({sumador_2_out_3, out_3[2]}));
  sumador4bits sumador_3 (
    .in_1({sumador_2_out_4[3], sumador_2_out_3}), .in_2(and_12_out), .out_4(out_3[7]), .out_3(out_3[6:3]));
endmodule

module Ejercicio10 (
  input  [7:0] y,
  input  [7:0] z,
  output [7:0] x
);

  wire [7:0] multiplier_1_out;

  Multiplier multiplier_1 (.a(y), .b(8'h2), .out(multiplier_1_out));  // open: cin, cout
  Adder adder_1 (.a(multiplier_1_out), .b(z), .out(x));  // open: cin, cout
endmodule
