// Logisim project Tarea4Etzael.circ as structural Verilog: 5 circuits, main circuit Sumador
module Sumador (
  input  A,
  input  B,
  input  C,
  output suma,
  output acarreo
);

  wire and_1_out, and_2_out, xor_1_out;

  xor xor_1 (xor_1_out, A, B);
  and and_1 (and_1_out, A, B);
  xor xor_2 (suma, xor_1_out, C);
  and and_2 (and_2_out, xor_1_out, C);
  or or_1 (acarreo, and_2_out, and_1_out);
endmodule

module Semi (
  input  A,
  input  B,
  output suma,
  output acarreo
);

  xor xor_1 (suma, A, B);
  and and_1 (acarreo, A, B);
endmodule

module Resta (
  input  [7:0] in_1,
  input  [7:0] in_2,
  output [7:0] out_3,
  output out_4
);

  wire semi_acarreo, sumador_2_acarreo, sumador_3_acarreo, sumador_4_acarreo, sumador_5_acarreo,
       sumador_6_acarreo, sumador_acarreo;

  Semi semi (.A(in_1[0]), .B(in_2[0]), .suma(out_3[0]), .acarreo(semi_acarreo));
  Sumador sumador (.A(semi_acarreo), .B(in_1[1]), .C(in_2[1]), .suma(out_3[1]), .acarreo(sumador_acarreo));
  Sumador sumador_2 (.A(sumador_acarreo), .B(in_1[2]), .C(in_2[2]), .suma(out_3[2]), .acarreo(sumador_2_acarreo));
  Sumador sumador_3 (.A(sumador_2_acarreo), .B(in_1[3]), .C(in_2[3]), .suma(out_3[3]), .acarreo(sumador_3_acarreo));
  Sumador sumador_4 (.A(sumador_3_acarreo), .B(in_1[4]), .C(in_2[4]), .suma(out_3[4]), .acarreo(sumador_4_acarreo));
  Sumador sumador_5 (.A(sumador_4_acarreo), .B(in_1[5]), .C(in_2[5]), .suma(out_3[5]), .acarreo(sumador_5_acarreo));
  Sumador sumador_6 (.A(sumador_5_acarreo), .B(in_1[6]), .C(in_2[6]), .suma(out_3[6]), .acarreo(sumador_6_acarreo));
  Sumador sumador_7 (.A(sumador_6_acarreo), .B(in_1[7]), .C(in_2[7]), .suma(out_3[7]), .acarreo(out_4));
endmodule

module Funcion1 (
  input  in_1,
  input  in_2,
  input  in_3,
  output out_4,
  output out_5
);

  wire and_1_out, and_2_out, and_3_out, nand_1_out, not_1_out, not_2_out, not_3_out;

  not not_1 (not_1_out, in_1);
  not not_2 (not_2_out, in_2);
  not not_3 (not_3_out, in_3);
  and and_1 (and_1_out, not_1_out, not_2_out, in_3);
  and and_2 (and_2_out, in_1, in_2, in_3);
  nand nand_1 (nand_1_out, in_1, in_2, in_3);
  and and_3 (and_3_out, in_1, in_2, not_3_out);
  or or_1 (out_5, and_1_out, and_2_out, nand_1_out, and_3_out);

  assign out_4 = 1'b1;

  // Notes on the sheet:
  //   Versión reducida
  //   Función original
endmodule

module Funcion2 (
  input  in_1,
  input  in_2,
  input  in_3,
  input  in_4,
  input  in_5,
  input  in_6,
  input  in_7,
  input  in_8,
  output out_9,
  output out_10
);

  wire and_1_out, and_2_out, and_3_out, and_4_out, nand_2_out, not_1_out, not_2_out, not_3_out, not_4_out;

  nand nand_1 (out_9, in_1, in_2, in_3, in_4);
  nand nand_2 (nand_2_out, in_5, in_6, in_7, in_8);
  not not_1 (not_1_out, in_5);
  not not_2 (not_2_out, in_6);
  not not_3 (not_3_out, in_7);
  and and_1 (and_1_out, not_1_out, not_2_out, not_3_out, in_8);
  and and_2 (and_2_out, not_1_out, not_2_out, in_7, in_8);
  not not_4 (not_4_out, in_7);
  and and_3 (and_3_out, in_5, in_6, not_3_out, not_4_out);
  and and_4 (and_4_out, in_5, in_6, in_7, not_4_out);
  or or_1 (out_10, nand_2_out, and_1_out, and_2_out, and_3_out, and_4_out);

  // Notes on the sheet:
  //   Versión reducida
  //   Función original
endmodule
